// Logisim project Cpu.circ as structural Verilog
module main (
  input  [15:0] in_1,
  input  in_2,
  input  in_3,
  input  in_4,
  input  [15:0] in_5,
  input  in_6,
  input  in_7,
  input  [1:0] in_8,
  input  [15:0] in_9,
  input  in_10,
  input  in_11,
  input  [15:0] in_12,
  input  [1:0] in_13,
  input  in_14,
  input  in_15,
  input  in_16,
  input  [3:0] in_17,
  input  in_18,
  input  [3:0] in_19,
  input  [4:0] alu_opcode,
  output [15:0] alu_inputA,
  output [15:0] alu_inputB,
  output [15:0] out_23,
  output JMP
);

  wire adder_1_cout, and_2_out, clk_out, comparator_1_gt, comparator_1_lt, comparator_2_eq, comparator_2_lt,
       comparator_3_eq, comparator_3_gt, comparator_3_lt, comparator_4_gt, decoder_1_out0, decoder_1_out1,
       decoder_1_out2, decoder_1_out3, decoder_1_out4, decoder_1_out5, decoder_1_out6, decoder_1_out7,
       decoder_1_out8, decoder_1_out9, decoder_1_out10, decoder_1_out11, decoder_1_out12, decoder_1_out13,
       decoder_1_out14, decoder_1_out15, decoder_2_out0, decoder_2_out1, decoder_2_out2, decoder_2_out3,
       decoder_2_out4, decoder_2_out5, decoder_2_out6, decoder_2_out7, decoder_2_out8, decoder_2_out9,
       decoder_2_out10, decoder_2_out11, decoder_2_out12, decoder_2_out13, decoder_2_out14, decoder_2_out15,
       or_1_out, or_2_out, or_3_out, or_4_out, or_5_out, or_6_out, or_7_out, or_8_out, or_9_out, or_10_out,
       or_11_out, or_12_out, or_13_out, or_14_out, or_15_out, or_16_out, or_19_out, or_20_out, or_21_out,
       or_22_out, subtractor_1_bout;
  wire [15:0] accumulator_r13_output_reg, adder_1_out, and_1_out, divider_1_out,
       Jump_target_reg_r12_output_reg, memory_address_register_r15_output_reg, multiplexer_3_out,
       multiplexer_4_out, multiplexer_5_out, multiplier_1_cout, multiplier_1_out, not_1_out, or_17_out,
       or_18_out, r0_output_reg, r1_output_reg, r2_output_reg, r3_output_reg, r4_output_reg, r5_output_reg,
       r6_output_reg, r7_output_reg, r8_output_reg, r9_output_reg, r10_output_reg, r11_output_reg,
       registerwithreadenable_1_output_reg, registerwithreadenable_2_output_reg,
       registerwithreadenable_3_output_reg, registerwithreadenable_4_output_reg, shifter_1_out,
       shifter_2_out, stack_ptr_r14_output_reg, subtractor_1_out;

  Decoder #(.select(4)) decoder_1 (
    .out0(decoder_1_out0), .out1(decoder_1_out1), .out2(decoder_1_out2), .out3(decoder_1_out3),
    .out4(decoder_1_out4), .out5(decoder_1_out5), .out6(decoder_1_out6), .out7(decoder_1_out7),
    .out8(decoder_1_out8), .out9(decoder_1_out9), .out10(decoder_1_out10), .out11(decoder_1_out11),
    .out12(decoder_1_out12), .out13(decoder_1_out13), .out14(decoder_1_out14), .out15(decoder_1_out15),
    .sel(in_17), .en(in_16));
  Decoder #(.select(4)) decoder_2 (
    .out0(decoder_2_out0), .out1(decoder_2_out1), .out2(decoder_2_out2), .out3(decoder_2_out3),
    .out4(decoder_2_out4), .out5(decoder_2_out5), .out6(decoder_2_out6), .out7(decoder_2_out7),
    .out8(decoder_2_out8), .out9(decoder_2_out9), .out10(decoder_2_out10), .out11(decoder_2_out11),
    .out12(decoder_2_out12), .out13(decoder_2_out13), .out14(decoder_2_out14), .out15(decoder_2_out15),
    .sel(in_19), .en(in_18));
  registerwithreadenable registerwithreadenable_1 (
    .data_reg(in_1), .write_enable_reg(in_2), .clock_reg(in_4), .read_enable_reg(in_3),
    .output_reg(registerwithreadenable_1_output_reg));
  registerwithreadenable registerwithreadenable_2 (
    .data_reg(in_5), .write_enable_reg(in_6), .clock_reg(in_4), .read_enable_reg(in_7),
    .output_reg(registerwithreadenable_2_output_reg));
  registerwithreadenable registerwithreadenable_3 (
    .data_reg(in_9), .write_enable_reg(in_10), .clock_reg(in_4), .read_enable_reg(in_11),
    .output_reg(registerwithreadenable_3_output_reg));
  registerwithreadenable registerwithreadenable_4 (
    .data_reg(in_12), .write_enable_reg(in_14), .clock_reg(in_4), .read_enable_reg(in_15),
    .output_reg(registerwithreadenable_4_output_reg));
  Multiplexer #(.select(2), .width(16)) multiplexer_1 (
    .in0(registerwithreadenable_1_output_reg), .in1(registerwithreadenable_2_output_reg),
    .in2(registerwithreadenable_3_output_reg), .in3(registerwithreadenable_4_output_reg), .out(alu_inputA),
    .sel(in_8));
  Multiplexer #(.select(2), .width(16)) multiplexer_2 (
    .in0(registerwithreadenable_1_output_reg), .in1(registerwithreadenable_2_output_reg),
    .in2(registerwithreadenable_3_output_reg), .in3(registerwithreadenable_4_output_reg), .out(alu_inputB),
    .sel(in_13));
  or or_1 (or_1_out, decoder_1_out0, decoder_2_out0);
  or or_2 (or_2_out, decoder_1_out1, decoder_2_out1);
  or or_3 (or_3_out, decoder_1_out2, decoder_2_out2);
  or or_4 (or_4_out, decoder_1_out3, decoder_2_out3);
  or or_5 (or_5_out, decoder_1_out4, decoder_2_out4);
  or or_6 (or_6_out, decoder_1_out5, decoder_2_out5);
  or or_7 (or_7_out, decoder_1_out10, decoder_2_out10);
  or or_8 (or_8_out, decoder_1_out11, decoder_2_out11);
  or or_9 (or_9_out, decoder_1_out12, decoder_2_out12);
  or or_10 (or_10_out, decoder_1_out13, decoder_2_out13);
  or or_11 (or_11_out, decoder_1_out14, decoder_2_out14);
  or or_12 (or_12_out, decoder_1_out15, decoder_2_out15);
  or or_13 (or_13_out, decoder_1_out6, decoder_2_out6);
  or or_14 (or_14_out, decoder_1_out7, decoder_2_out7);
  or or_15 (or_15_out, decoder_1_out8, decoder_2_out8);
  or or_16 (or_16_out, decoder_1_out9, decoder_2_out9);
  Clock clk (.out(clk_out));
  // RGB_Video #(.height(192), .scale(3), .width(256)) rgb_video_1: pin names not known
  registerwithreadenable r0 (
    .data_reg(out_23), .clock_reg(clk_out), .read_enable_reg(or_1_out), .output_reg(r0_output_reg));  // open: write_enable_reg
  registerwithreadenable r1 (
    .data_reg(out_23), .clock_reg(clk_out), .read_enable_reg(or_2_out), .output_reg(r1_output_reg));  // open: write_enable_reg
  registerwithreadenable r2 (
    .data_reg(out_23), .clock_reg(clk_out), .read_enable_reg(or_3_out), .output_reg(r2_output_reg));  // open: write_enable_reg
  registerwithreadenable r3 (
    .data_reg(out_23), .clock_reg(clk_out), .read_enable_reg(or_4_out), .output_reg(r3_output_reg));  // open: write_enable_reg
  registerwithreadenable r4 (
    .data_reg(out_23), .clock_reg(clk_out), .read_enable_reg(or_5_out), .output_reg(r4_output_reg));  // open: write_enable_reg
  registerwithreadenable r5 (
    .data_reg(out_23), .clock_reg(clk_out), .read_enable_reg(or_6_out), .output_reg(r5_output_reg));  // open: write_enable_reg
  registerwithreadenable r6 (
    .data_reg(out_23), .clock_reg(clk_out), .read_enable_reg(or_13_out), .output_reg(r6_output_reg));  // open: write_enable_reg
  registerwithreadenable r7 (
    .data_reg(out_23), .clock_reg(clk_out), .read_enable_reg(or_14_out), .output_reg(r7_output_reg));  // open: write_enable_reg
  registerwithreadenable r8 (
    .data_reg(out_23), .clock_reg(clk_out), .read_enable_reg(or_15_out), .output_reg(r8_output_reg));  // open: write_enable_reg
  registerwithreadenable r9 (
    .data_reg(out_23), .clock_reg(clk_out), .read_enable_reg(or_16_out), .output_reg(r9_output_reg));  // open: write_enable_reg
  registerwithreadenable r11 (
    .data_reg(out_23), .clock_reg(clk_out), .read_enable_reg(or_8_out), .output_reg(r11_output_reg));  // open: write_enable_reg
  Pull_Resistor pull_resistor_1 (.node(out_23));
  registerwithreadenable r10 (
    .data_reg(out_23), .clock_reg(clk_out), .output_reg(r10_output_reg));  // open: write_enable_reg, read_enable_reg
  Multiplexer #(.select(4), .width(16)) multiplexer_3 (
    .in0(r0_output_reg), .in1(r1_output_reg), .in2(r2_output_reg), .in3(r3_output_reg), .in4(r4_output_reg),
    .in5(r5_output_reg), .in6(r6_output_reg), .in7(r7_output_reg), .in8(r8_output_reg), .in9(r9_output_reg),
    .in10(r10_output_reg), .in11(r11_output_reg), .in12(Jump_target_reg_r12_output_reg),
    .in13(accumulator_r13_output_reg), .in14(stack_ptr_r14_output_reg),
    .in15(memory_address_register_r15_output_reg), .out(multiplexer_3_out), .sel(in_17));
  Multiplexer #(.select(4), .width(16)) multiplexer_4 (
    .in0(r0_output_reg), .in1(r1_output_reg), .in2(r2_output_reg), .in3(r3_output_reg), .in4(r4_output_reg),
    .in5(r5_output_reg), .in6(r6_output_reg), .in7(r7_output_reg), .in8(r8_output_reg), .in9(r9_output_reg),
    .in10(r10_output_reg), .in11(r11_output_reg), .in12(Jump_target_reg_r12_output_reg),
    .in13(accumulator_r13_output_reg), .in14(stack_ptr_r14_output_reg),
    .in15(memory_address_register_r15_output_reg), .out(multiplexer_4_out), .sel(in_19));
  Register #(.width(1)) JZ (.D(comparator_3_eq), .en(and_2_out), .clk(clk_out));  // open: Q, clr
  ROM #(.addrWidth(16), .dataWidth(16)) Program_memory ();  // open: addr, data
  Register #(.width(1)) JG (.D(comparator_3_gt), .en(and_2_out));  // open: clk, Q, clr
  Register #(.width(1)) JS (.D(comparator_3_lt), .en(and_2_out));  // open: clk, Q, clr
  registerwithreadenable memory_address_register_r15 (
    .data_reg(out_23), .clock_reg(clk_out), .read_enable_reg(or_12_out),
    .output_reg(memory_address_register_r15_output_reg));  // open: write_enable_reg
  registerwithreadenable Jump_target_reg_r12 (
    .data_reg(out_23), .clock_reg(clk_out), .read_enable_reg(or_9_out),
    .output_reg(Jump_target_reg_r12_output_reg));  // open: write_enable_reg
  Register #(.width(1)) JO (.D(or_22_out), .en(and_2_out));  // open: clk, Q, clr
  registerwithreadenable accumulator_r13 (
    .data_reg(multiplexer_5_out), .write_enable_reg(and_2_out), .clock_reg(clk_out),
    .read_enable_reg(or_10_out), .output_reg(accumulator_r13_output_reg));
  registerwithreadenable stack_ptr_r14 (
    .data_reg(out_23), .clock_reg(clk_out), .read_enable_reg(or_11_out), .output_reg(stack_ptr_r14_output_reg));  // open: write_enable_reg
  Register #(.width(1)) JV ();  // open: D, en, clk, Q, clr
  // DualRAM #(.addrWidth(16), .dataWidth(16)) data_memory: pin names not known
  Comparator #(.width(5)) comparator_1 (
    .a(alu_opcode), .b(5'b00001), .gt(comparator_1_gt), .lt(comparator_1_lt));  // open: eq
  Comparator #(.width(5)) comparator_2 (
    .a(alu_opcode), .b(5'b01101), .eq(comparator_2_eq), .lt(comparator_2_lt));  // open: gt
  Adder #(.width(16)) adder_1 (
    .a(multiplexer_3_out), .b(multiplexer_4_out), .out(adder_1_out), .cout(adder_1_cout));  // open: cin
  Subtractor #(.width(16)) subtractor_1 (
    .a(multiplexer_3_out), .b(multiplexer_4_out), .out(subtractor_1_out), .bout(subtractor_1_bout));  // open: bin
  Multiplier #(.mode("twosComplement"), .width(16)) multiplier_1 (
    .a(multiplexer_3_out), .b(multiplexer_4_out), .out(multiplier_1_out), .cout(multiplier_1_cout));  // open: cin
  Divider #(.mode("twosComplement"), .width(16)) divider_1 (
    .a(multiplexer_3_out), .b(multiplexer_4_out), .out(divider_1_out));  // open: upper, rem
  assign and_1_out = multiplexer_3_out & multiplexer_4_out;  // AND_Gate and_1, 16 bits wide
  assign or_17_out = multiplexer_3_out | multiplexer_4_out;  // OR_Gate or_17, 16 bits wide
  assign or_18_out = multiplexer_3_out | multiplexer_4_out;  // OR_Gate or_18, 16 bits wide
  assign not_1_out = ~multiplexer_3_out;  // NOT_Gate not_1, 16 bits wide
  Shifter #(.width(16)) shifter_1 (.in(multiplexer_3_out), .\dist (multiplexer_4_out[3:0]), .out(shifter_1_out));
  Shifter #(.shift("lr"), .width(16)) shifter_2 (
    .in(multiplexer_3_out), .\dist (multiplexer_4_out[3:0]), .out(shifter_2_out));
  Comparator #(.width(16)) comparator_3 (
    .a(multiplexer_3_out), .b(multiplexer_4_out), .gt(comparator_3_gt), .eq(comparator_3_eq),
    .lt(comparator_3_lt));
  or or_19 (or_19_out, comparator_1_gt, comparator_1_lt);
  or or_20 (or_20_out, comparator_2_eq, comparator_2_lt);
  and and_2 (and_2_out, or_19_out, or_20_out);
  Multiplexer #(.select(5), .width(16)) multiplexer_5 (
    .in1(adder_1_out), .in2(subtractor_1_out), .in3(multiplier_1_out), .in4(divider_1_out), .in5(and_1_out),
    .in6(or_17_out), .in7(or_18_out), .in8(not_1_out), .in9(shifter_1_out), .in10(shifter_2_out),
    .out(multiplexer_5_out), .sel(alu_opcode));  // open: in0, in11, in12, in13, in14, in15, in16, in17, in18, in19, in20, in21, in22, in23, in24, in25, in26, in27, in28, in29, in30, in31
  or or_21 (or_21_out, adder_1_cout, subtractor_1_bout);
  Comparator #(.width(16)) comparator_4 (.a(multiplier_1_cout), .b({16{1'b0}}), .gt(comparator_4_gt));  // open: eq, lt
  or or_22 (or_22_out, or_21_out, comparator_4_gt);

  // Notes on the sheet:
  //   Src1
  //   Src2
endmodule

module registerwithreadenable (
  input  [15:0] data_reg,
  input  write_enable_reg,
  input  clock_reg,
  input  read_enable_reg,
  output [15:0] output_reg
);

  wire [15:0] register_1_q;

  Register #(.width(16)) register_1 (
    .D(data_reg), .en(write_enable_reg), .clk(clock_reg), .Q(register_1_q));  // open: clr
  Multiplexer #(.width(16)) multiplexer_1 (.in1(register_1_q), .out(output_reg), .sel(read_enable_reg));  // open: in0
endmodule
